// Digital circuit Microprocessor_Complete.dig as structural Verilog
module Microprocessor_Complete (
  input  [3:0] data__in,
  input  reset,
  input  clk,
  output [3:0] accum
);

  wire not_1_out;
  wire [1:0] step__reg;
  wire [3:0] addr__bus, alu__out, data__bus, data__mux_y, instr__reg, mar, pc, program_ram_1_data__out;
  wire [13:0] rom__out;

  four_bit_reg Instruction_Reg (.d(data__bus), .enable(rom__out[0]), .reset(reset), .clk(clk), .q(instr__reg));
  two_bit_reg Step_Reg (.d(rom__out[13:12]), .enable(1'b1), .reset(reset), .clk(clk), .q(step__reg));
  program_ctr program_ctr_1 (.enable(rom__out[9]), .reset(reset), .clk(clk), .q(pc));
  four_bit_reg u_MAR (.d(data__bus), .enable(rom__out[8]), .reset(reset), .clk(clk), .q(mar));
  not not_1 (not_1_out, rom__out[9]);
  ROM microcode_ROM (.A(step__reg), .sel(1'b1), .D(rom__out[0]));
  four_bit_mux four_bit_mux_1 (.a(pc), .b(mar), .sel(not_1_out), .y(addr__bus));
  alu alu_1 (
    .a(data__bus), .b(accum), .invert(rom__out[6]), .arith(rom__out[7]), .pass(rom__out[5]), .cin(1'b0),
    .y(alu__out));  // open: cout, overfl
  four_bit_reg accumulator (.d(alu__out), .enable(rom__out[4]), .reset(reset), .clk(clk), .q(accum));
  four_bit_mux accum__mux (.a(data__mux_y), .b(accum), .sel(rom__out[3]), .y(data__bus));
  program_ram program_ram_1 (
    .addr(addr__bus), .data__in(data__bus), .clk(clk), .write(rom__out[1]),
    .data__out(program_ram_1_data__out));
  four_bit_mux data__mux (.a(data__in), .b(program_ram_1_data__out), .sel(rom__out[2]), .y(data__mux_y));
  // Pins of 1 and 14 bits meet at rom__out
  // Pins of 2 and 6 bits meet at {instr__reg, step__reg}
endmodule
