// Digital circuit not_neg.dig as structural Verilog
module not_neg (
  input  [3:0] a,
  input  invert,
  input  neg,
  output [3:0] y,
  output cry
);

  wire and_1_out;
  wire [3:0] xor_1_out;

  xor xor_1 (xor_1_out[0], a[0], invert);
  xor xor_2 (xor_1_out[1], a[1], invert);
  xor xor_3 (xor_1_out[2], a[2], invert);
  xor xor_4 (xor_1_out[3], a[3], invert);
  and and_1 (and_1_out, invert, neg);
  incrementer incrementer_1 (.a(xor_1_out), .inc(and_1_out), .y(y), .cry(cry));
endmodule
